// Logisim project Cpu.circ as structural Verilog: 7 circuits, main circuit main
module main (
  input  [4:0] in_1,
  input  in_2,
  input  [4:0] in_3,
  input  in_4,
  input  [31:0] in_5
);

  wire clock_1_out, not_1_out;
  wire [7:0] controlled_buffer_1_out, controlled_buffer_1_out_2, controlled_buffer_1_out_3,
       controlled_buffer_1_out_4;

  Clock clock_1 (.out(clock_1_out));
  not not_1 (not_1_out, in_4);
  assign {controlled_buffer_1_out_4, controlled_buffer_1_out_3, controlled_buffer_1_out_2, controlled_buffer_1_out} = not_1_out ? in_5 : 32'bz;  // Controlled_Buffer controlled_buffer_1
  LedBar ledbar_1 (
    .led0(controlled_buffer_1_out_4[7]), .led1(controlled_buffer_1_out_4[6]),
    .led2(controlled_buffer_1_out_4[5]), .led3(controlled_buffer_1_out_4[4]),
    .led4(controlled_buffer_1_out_4[3]), .led5(controlled_buffer_1_out_4[2]),
    .led6(controlled_buffer_1_out_4[1]), .led7(controlled_buffer_1_out_4[0]));
  LedBar ledbar_2 (
    .led0(controlled_buffer_1_out_3[7]), .led1(controlled_buffer_1_out_3[6]),
    .led2(controlled_buffer_1_out_3[5]), .led3(controlled_buffer_1_out_3[4]),
    .led4(controlled_buffer_1_out_3[3]), .led5(controlled_buffer_1_out_3[2]),
    .led6(controlled_buffer_1_out_3[1]), .led7(controlled_buffer_1_out_3[0]));
  LedBar ledbar_3 (
    .led0(controlled_buffer_1_out_2[7]), .led1(controlled_buffer_1_out_2[6]),
    .led2(controlled_buffer_1_out_2[5]), .led3(controlled_buffer_1_out_2[4]),
    .led4(controlled_buffer_1_out_2[3]), .led5(controlled_buffer_1_out_2[2]),
    .led6(controlled_buffer_1_out_2[1]), .led7(controlled_buffer_1_out_2[0]));
  MainRegisters mainregisters_1 (
    .WriteSelect(in_1), .WriteEnable(in_2), .ReadSelect(in_3), .ReadEnable(in_4), .CLK(clock_1_out),
    .InData({controlled_buffer_1_out_4, controlled_buffer_1_out_3, controlled_buffer_1_out_2, controlled_buffer_1_out}),
    .OutData({controlled_buffer_1_out_4, controlled_buffer_1_out_3, controlled_buffer_1_out_2, controlled_buffer_1_out}));
  LedBar ledbar_4 (
    .led0(controlled_buffer_1_out[7]), .led1(controlled_buffer_1_out[6]), .led2(controlled_buffer_1_out[5]),
    .led3(controlled_buffer_1_out[4]), .led4(controlled_buffer_1_out[3]), .led5(controlled_buffer_1_out[2]),
    .led6(controlled_buffer_1_out[1]), .led7(controlled_buffer_1_out[0]));
endmodule

module ByteRegister (
  input  nWrite,
  input  nRead,
  input  CLK,
  input  [7:0] InData,
  output [7:0] OutData
);

  wire n74245_1_pin1, n74377_1_pin2, n74377_1_pin5, n74377_1_pin6, n74377_1_pin9, n74377_1_pin12,
       n74377_1_pin15, n74377_1_pin16, n74377_1_pin19;

  _74377 u_74377_1 (
    .pin1(nWrite), .pin2(n74377_1_pin2), .pin3(InData[0]), .pin4(InData[1]), .pin5(n74377_1_pin5),
    .pin6(n74377_1_pin6), .pin7(InData[2]), .pin8(InData[3]), .pin9(n74377_1_pin9), .pin19(n74377_1_pin19),
    .pin18(InData[4]), .pin17(InData[5]), .pin16(n74377_1_pin16), .pin15(n74377_1_pin15), .pin14(InData[6]),
    .pin13(InData[7]), .pin12(n74377_1_pin12), .pin11(CLK));
  _74245 u_74245_1 (
    .pin1(n74245_1_pin1), .pin2(n74377_1_pin2), .pin3(n74377_1_pin5), .pin4(n74377_1_pin6),
    .pin5(n74377_1_pin9), .pin6(n74377_1_pin19), .pin7(n74377_1_pin16), .pin8(n74377_1_pin15),
    .pin9(n74377_1_pin12), .pin19(nRead), .pin18(OutData[0]), .pin17(OutData[1]), .pin16(OutData[2]),
    .pin15(OutData[3]), .pin14(OutData[4]), .pin13(OutData[5]), .pin12(OutData[6]), .pin11(OutData[7]));
  // also tied to VCC on the sheet: n74245_1_pin1
endmodule

module WordRegister (
  input  nWrite,
  input  nRead,
  input  CLK,
  input  [31:0] InData,
  output [31:0] OutData
);

  ByteRegister byteregister_1 (.nWrite(nWrite), .nRead(nRead), .CLK(CLK), .InData(InData[7:0]), .OutData(OutData[7:0]));
  ByteRegister byteregister_2 (
    .nWrite(nWrite), .nRead(nRead), .CLK(CLK), .InData(InData[15:8]), .OutData(OutData[15:8]));
  ByteRegister byteregister_3 (
    .nWrite(nWrite), .nRead(nRead), .CLK(CLK), .InData(InData[23:16]), .OutData(OutData[23:16]));
  ByteRegister byteregister_4 (
    .nWrite(nWrite), .nRead(nRead), .CLK(CLK), .InData(InData[31:24]), .OutData(OutData[31:24]));
endmodule

module MainRegisters (
  input  [4:0] WriteSelect,
  input  WriteEnable,
  input  [4:0] ReadSelect,
  input  ReadEnable,
  input  CLK,
  input  [31:0] InData,
  output [31:0] OutData
);

  wire [31:0] registerselector_1_out_3, registerselector_2_out_3;

  RegisterSelector registerselector_1 (.Index(WriteSelect), .Enable(WriteEnable), .out_3(registerselector_1_out_3));
  RegisterSelector registerselector_2 (.Index(ReadSelect), .Enable(ReadEnable), .out_3(registerselector_2_out_3));
  ZeroRegister zeroregister_1 (
    .nWrite(registerselector_1_out_3[0]), .nRead(registerselector_2_out_3[0]), .InData(InData),
    .OutData(OutData));
  WordRegister wordregister_1 (
    .nWrite(registerselector_1_out_3[1]), .nRead(registerselector_2_out_3[1]), .CLK(CLK), .InData(InData),
    .OutData(OutData));
  WordRegister wordregister_2 (
    .nWrite(registerselector_1_out_3[2]), .nRead(registerselector_2_out_3[2]), .CLK(CLK), .InData(InData),
    .OutData(OutData));
  WordRegister wordregister_3 (
    .nWrite(registerselector_1_out_3[3]), .nRead(registerselector_2_out_3[3]), .CLK(CLK), .InData(InData),
    .OutData(OutData));
  WordRegister wordregister_4 (
    .nWrite(registerselector_1_out_3[4]), .nRead(registerselector_2_out_3[4]), .CLK(CLK), .InData(InData),
    .OutData(OutData));
  WordRegister wordregister_5 (
    .nWrite(registerselector_1_out_3[5]), .nRead(registerselector_2_out_3[5]), .CLK(CLK), .InData(InData),
    .OutData(OutData));
  WordRegister wordregister_6 (
    .nWrite(registerselector_1_out_3[6]), .nRead(registerselector_2_out_3[6]), .CLK(CLK), .InData(InData),
    .OutData(OutData));
  WordRegister wordregister_7 (
    .nWrite(registerselector_1_out_3[7]), .nRead(registerselector_2_out_3[7]), .CLK(CLK), .InData(InData),
    .OutData(OutData));
  WordRegister wordregister_8 (
    .nWrite(registerselector_1_out_3[8]), .nRead(registerselector_2_out_3[8]), .CLK(CLK), .InData(InData),
    .OutData(OutData));
  WordRegister wordregister_9 (
    .nWrite(registerselector_1_out_3[9]), .nRead(registerselector_2_out_3[9]), .CLK(CLK), .InData(InData),
    .OutData(OutData));
  WordRegister wordregister_10 (
    .nWrite(registerselector_1_out_3[10]), .nRead(registerselector_2_out_3[10]), .CLK(CLK), .InData(InData),
    .OutData(OutData));
  WordRegister wordregister_11 (
    .nWrite(registerselector_1_out_3[11]), .nRead(registerselector_2_out_3[11]), .CLK(CLK), .InData(InData),
    .OutData(OutData));
  WordRegister wordregister_12 (
    .nWrite(registerselector_1_out_3[12]), .nRead(registerselector_2_out_3[12]), .CLK(CLK), .InData(InData),
    .OutData(OutData));
  WordRegister wordregister_13 (
    .nWrite(registerselector_1_out_3[13]), .nRead(registerselector_2_out_3[13]), .CLK(CLK), .InData(InData),
    .OutData(OutData));
  WordRegister wordregister_14 (
    .nWrite(registerselector_1_out_3[14]), .nRead(registerselector_2_out_3[14]), .CLK(CLK), .InData(InData),
    .OutData(OutData));
  WordRegister wordregister_15 (
    .nWrite(registerselector_1_out_3[15]), .nRead(registerselector_2_out_3[15]), .CLK(CLK), .InData(InData),
    .OutData(OutData));
  WordRegister wordregister_16 (
    .nWrite(registerselector_1_out_3[16]), .nRead(registerselector_2_out_3[16]), .CLK(CLK), .InData(InData),
    .OutData(OutData));
  WordRegister wordregister_17 (
    .nWrite(registerselector_1_out_3[17]), .nRead(registerselector_2_out_3[17]), .CLK(CLK), .InData(InData),
    .OutData(OutData));
  WordRegister wordregister_18 (
    .nWrite(registerselector_1_out_3[18]), .nRead(registerselector_2_out_3[18]), .CLK(CLK), .InData(InData),
    .OutData(OutData));
  WordRegister wordregister_19 (
    .nWrite(registerselector_1_out_3[19]), .nRead(registerselector_2_out_3[19]), .CLK(CLK), .InData(InData),
    .OutData(OutData));
  WordRegister wordregister_20 (
    .nWrite(registerselector_1_out_3[20]), .nRead(registerselector_2_out_3[20]), .CLK(CLK), .InData(InData),
    .OutData(OutData));
  WordRegister wordregister_21 (
    .nWrite(registerselector_1_out_3[21]), .nRead(registerselector_2_out_3[21]), .CLK(CLK), .InData(InData),
    .OutData(OutData));
  WordRegister wordregister_22 (
    .nWrite(registerselector_1_out_3[22]), .nRead(registerselector_2_out_3[22]), .CLK(CLK), .InData(InData),
    .OutData(OutData));
  WordRegister wordregister_23 (
    .nWrite(registerselector_1_out_3[23]), .nRead(registerselector_2_out_3[23]), .CLK(CLK), .InData(InData),
    .OutData(OutData));
  WordRegister wordregister_24 (
    .nWrite(registerselector_1_out_3[24]), .nRead(registerselector_2_out_3[24]), .CLK(CLK), .InData(InData),
    .OutData(OutData));
  WordRegister wordregister_25 (
    .nWrite(registerselector_1_out_3[25]), .nRead(registerselector_2_out_3[25]), .CLK(CLK), .InData(InData),
    .OutData(OutData));
  WordRegister wordregister_26 (
    .nWrite(registerselector_1_out_3[26]), .nRead(registerselector_2_out_3[26]), .CLK(CLK), .InData(InData),
    .OutData(OutData));
  WordRegister wordregister_27 (
    .nWrite(registerselector_1_out_3[27]), .nRead(registerselector_2_out_3[27]), .CLK(CLK), .InData(InData),
    .OutData(OutData));
  WordRegister wordregister_28 (
    .nWrite(registerselector_1_out_3[28]), .nRead(registerselector_2_out_3[28]), .CLK(CLK), .InData(InData),
    .OutData(OutData));
  WordRegister wordregister_29 (
    .nWrite(registerselector_1_out_3[29]), .nRead(registerselector_2_out_3[29]), .CLK(CLK), .InData(InData),
    .OutData(OutData));
  WordRegister wordregister_30 (
    .nWrite(registerselector_1_out_3[30]), .nRead(registerselector_2_out_3[30]), .CLK(CLK), .InData(InData),
    .OutData(OutData));
  WordRegister wordregister_31 (
    .nWrite(registerselector_1_out_3[31]), .nRead(registerselector_2_out_3[31]), .CLK(CLK), .InData(InData),
    .OutData(OutData));
endmodule

module RegisterSelector (
  input  [4:0] Index,
  input  Enable,
  output [31:0] out_3
);

  wire n7404_1_pin10, n7404_1_pin12;

  _7404 u_7404_1 (
    .pin13(Index[3]), .pin12(n7404_1_pin12), .pin11(Index[4]), .pin10(n7404_1_pin10));  // open: pin1, pin2, pin3, pin4, pin5, pin6, pin9, pin8
  _74138 u_74138_1 (
    .pin1(Index[0]), .pin2(Index[1]), .pin3(Index[2]), .pin4(Index[3]), .pin5(Index[4]), .pin6(Enable),
    .pin7(out_3[7]), .pin15(out_3[0]), .pin14(out_3[1]), .pin13(out_3[2]), .pin12(out_3[3]),
    .pin11(out_3[4]), .pin10(out_3[5]), .pin9(out_3[6]));
  _74138 u_74138_2 (
    .pin1(Index[0]), .pin2(Index[1]), .pin3(Index[2]), .pin4(n7404_1_pin12), .pin5(Index[4]), .pin6(Enable),
    .pin7(out_3[15]), .pin15(out_3[8]), .pin14(out_3[9]), .pin13(out_3[10]), .pin12(out_3[11]),
    .pin11(out_3[12]), .pin10(out_3[13]), .pin9(out_3[14]));
  _74138 u_74138_3 (
    .pin1(Index[0]), .pin2(Index[1]), .pin3(Index[2]), .pin4(Index[3]), .pin5(n7404_1_pin10), .pin6(Enable),
    .pin7(out_3[23]), .pin15(out_3[16]), .pin14(out_3[17]), .pin13(out_3[18]), .pin12(out_3[19]),
    .pin11(out_3[20]), .pin10(out_3[21]), .pin9(out_3[22]));
  _74138 u_74138_4 (
    .pin1(Index[0]), .pin2(Index[1]), .pin3(Index[2]), .pin4(n7404_1_pin12), .pin5(n7404_1_pin10),
    .pin6(Enable), .pin7(out_3[31]), .pin15(out_3[24]), .pin14(out_3[25]), .pin13(out_3[26]),
    .pin12(out_3[27]), .pin11(out_3[28]), .pin10(out_3[29]), .pin9(out_3[30]));
endmodule

module ZeroRegister (
  input  nWrite,
  input  nRead,
  input  [31:0] InData,
  output [31:0] OutData
);

  wire n74245_1_pin1, n74245_1_pin2;

  // NoConnect on nWrite
  // NoConnect on InData
  _74245 u_74245_1 (
    .pin1(n74245_1_pin1), .pin2(n74245_1_pin2), .pin3(n74245_1_pin2), .pin4(n74245_1_pin2),
    .pin5(n74245_1_pin2), .pin6(n74245_1_pin2), .pin7(n74245_1_pin2), .pin8(n74245_1_pin2),
    .pin9(n74245_1_pin2), .pin19(nRead), .pin18(OutData[0]), .pin17(OutData[1]), .pin16(OutData[2]),
    .pin15(OutData[3]), .pin14(OutData[4]), .pin13(OutData[5]), .pin12(OutData[6]), .pin11(OutData[7]));
  _74245 u_74245_2 (
    .pin1(n74245_1_pin1), .pin2(n74245_1_pin2), .pin3(n74245_1_pin2), .pin4(n74245_1_pin2),
    .pin5(n74245_1_pin2), .pin6(n74245_1_pin2), .pin7(n74245_1_pin2), .pin8(n74245_1_pin2),
    .pin9(n74245_1_pin2), .pin19(nRead), .pin18(OutData[8]), .pin17(OutData[9]), .pin16(OutData[10]),
    .pin15(OutData[11]), .pin14(OutData[12]), .pin13(OutData[13]), .pin12(OutData[14]), .pin11(OutData[15]));
  _74245 u_74245_3 (
    .pin1(n74245_1_pin1), .pin2(n74245_1_pin2), .pin3(n74245_1_pin2), .pin4(n74245_1_pin2),
    .pin5(n74245_1_pin2), .pin6(n74245_1_pin2), .pin7(n74245_1_pin2), .pin8(n74245_1_pin2),
    .pin9(n74245_1_pin2), .pin19(nRead), .pin18(OutData[16]), .pin17(OutData[17]), .pin16(OutData[18]),
    .pin15(OutData[19]), .pin14(OutData[20]), .pin13(OutData[21]), .pin12(OutData[22]), .pin11(OutData[23]));
  _74245 u_74245_4 (
    .pin1(n74245_1_pin1), .pin2(n74245_1_pin2), .pin3(n74245_1_pin2), .pin4(n74245_1_pin2),
    .pin5(n74245_1_pin2), .pin6(n74245_1_pin2), .pin7(n74245_1_pin2), .pin8(n74245_1_pin2),
    .pin9(n74245_1_pin2), .pin19(nRead), .pin18(OutData[24]), .pin17(OutData[25]), .pin16(OutData[26]),
    .pin15(OutData[27]), .pin14(OutData[28]), .pin13(OutData[29]), .pin12(OutData[30]), .pin11(OutData[31]));
  // also tied to GND on the sheet: n74245_1_pin2
  // also tied to VCC on the sheet: n74245_1_pin1
endmodule

module RegisterDecoder (
  input  [31:0] Ins,
  output [4:0] RD,
  output [4:0] RS1,
  output [4:0] RS2
);


  assign RD = Ins[11:7];
  assign RS1 = Ins[19:15];
  assign RS2 = Ins[24:20];
endmodule
